# Fritzing sketch vegimeter2 (saved by Fritzing 0.8.7b)
circuit board: 14.8cm x 9cm
breadboards: 3

parts:
  Heater_Relay_1 = RELAY [package=relay-jzc]
  Pump_Relay = RELAY [package=relay-jzc]
  Air_Temp = TEMPERATURE-SENSOR [part_number=DS18B20 package=to-92]
  R8_1k = Resistor [tolerance=±5% resistance=1k package=THT]
  R11_4_7k = Resistor [tolerance=±5% resistance=4.7k package=THT]
  R6_1k = Resistor [tolerance=±5% resistance=1k package=THT]
  R12_1k = Resistor [tolerance=±5% resistance=1k package=THT]
  R9_1k = Resistor [tolerance=±5% resistance=1k package=THT]
  R4_220 = Resistor [tolerance=±5% resistance=220 package=THT]
  XBEE_In = LED - 5mm [color="Red (633nm)" package="5 mm [THT]"]
  XBEE_Out = LED - 5mm [color="Red (633nm)" package="5 mm [THT]"]
  R1_10k = Resistor [tolerance=±20% resistance=10k package=THT]
  C1_4_7uF = Electrolytic Capacitor [capacitance=4.7mF package="100 mil [THT, electrolytic]"]
  R2_1k = Resistor [tolerance=±5% resistance=1k package=THT]
  XBEE = XBee
  U1 = M10X2 [package=2x10_lock]
  U2 = M10X2 [package=2x10_lock]
  Heater_Relay_2 = RELAY [package=relay-jzc]
  Heater_Relay_3 = RELAY [package=relay-jzc]
  R10_1k = Resistor [tolerance=±5% resistance=1k package=THT]
  LR_3_3V = Voltage Regulator [package=to220-adj]
  R3_33k = Resistor [tolerance=±5% resistance=33k package=THT]
  MIC29302 = Voltage Regulator Adj 3A [part_number=mic29302wt package=to220-5]
  R7_1k = Resistor [tolerance=±5% resistance=1k package=THT]
  ULN2803A = ULN2803A [package=THT]
  Water_B = Molex 3 Pin header 3.96mm
  Water_A = Molex 3 Pin header 3.96mm
  Soil_B = Molex 3 Pin header 3.96mm
  Soil_A = Molex 3 Pin header 3.96mm
  Soil_C = Molex 3 Pin header 3.96mm
  Soil_D = Molex 3 Pin header 3.96mm
  Pump = Molex 3 Pin header 3.96mm
  C2_10uF = Electrolytic Capacitor [capacitance=10µF package="100 mil [THT, electrolytic]"]
  Heater = Molex Sabre 2 Pin Power [part_number=MOLEX-43160-0102 package=MOLEX-WIRE-BOARD-CONNECTOR-HEADER-2POS-7.5MM]
  Primary_Power = Molex Sabre 2 Pin Power [part_number=MOLEX-43160-0102 package=MOLEX-WIRE-BOARD-CONNECTOR-HEADER-2POS-7.5MM]
  R5_220 = Resistor [tolerance=±5% resistance=220 package=THT]

nets (from the pcb view):
  N1: Heater_Relay_1.COIL2, Pump_Relay.COIL2, Heater_Relay_2.COIL2, Heater_Relay_3.COIL2, R3_33k.Pin_1, MIC29302.pin_4, Pump.1, C2_10uF.+
  N2: Heater_Relay_1.NO, Heater_Relay_2.NO, Heater_Relay_3.NO, Heater.1
  GND: Heater_Relay_1.MAIN, Pump_Relay.MAIN, Air_Temp.GND, R1_10k.Pin_1, C1_4_7uF.-, XBEE.GND, U2.19, Heater_Relay_2.MAIN, Heater_Relay_3.MAIN, LR_3_3V.ADJ, MIC29302.Pin_3, ULN2803A.0V, Water_B.1, Water_A.1, Soil_B.1, Soil_A.1, Soil_C.1, Soil_D.1, C2_10uF.-, Primary_Power.1
  N3: Heater_Relay_1.COIL1, ULN2803A.Out_8, ULN2803A.Out_7
  N4: Pump_Relay.NO, Pump.3
  N5: Pump_Relay.COIL1, ULN2803A.Out_2, ULN2803A.Out_1
  N6: Air_Temp.ADJ, R11_4_7k.Pin_1, U1.9
  VCC: Air_Temp.VCC, R8_1k.Pin_0, R11_4_7k.Pin_0, R6_1k.Pin_0, R12_1k.Pin_0, R9_1k.Pin_0, XBEE_In.cathode, XBEE_Out.cathode, XBEE.VCC, U2.18, R10_1k.Pin_0, LR_3_3V.OUT, R7_1k.Pin_0, Water_B.3, Water_A.3, Soil_B.3, Soil_A.3, Soil_C.3, Soil_D.3
  N7: R8_1k.Pin_1, U1.15, Soil_C.2
  N8: R6_1k.Pin_1, U1.11, Soil_A.2
  N9: R12_1k.Pin_1, U1.10, Water_B.2
  N10: R9_1k.Pin_1, U1.13, Soil_D.2
  N11: R4_220.Pin_0, XBEE_In.anode
  N12: R4_220.Pin_1, XBEE.pin3, U2.6
  N13: XBEE_Out.anode, R5_220.Pin_0
  N14: R1_10k.Pin_0, R2_1k.Pin_1
  N15: C1_4_7uF.+, LR_3_3V.IN, MIC29302.Pin_1, MIC29302.Pin_2, ULN2803A.COM_-_Common, Heater.2, Primary_Power.2
  N16: R2_1k.Pin_0, R3_33k.Pin_0, MIC29302.Pin_5
  N17: XBEE.pin2, U2.5, R5_220.Pin_1
  N18: U1.12, R10_1k.Pin_1, Water_A.2
  N19: U1.14, R7_1k.Pin_1, Soil_B.2
  N20: U1.16, ULN2803A.In_3, ULN2803A.In_4, ULN2803A.In_5, ULN2803A.In_6, ULN2803A.In_7, ULN2803A.In_8
  N21: U2.7, ULN2803A.In_1, ULN2803A.In_2
  N22: Heater_Relay_2.COIL1, ULN2803A.Out_6, ULN2803A.Out_5
  N23: Heater_Relay_3.COIL1, ULN2803A.Out_4, ULN2803A.Out_3

notes:
  Vegimeter 2
  Rev 3
  www.bionicbunny.org
  (-)
  (+)

custom parts:
  Voltage Regulator Adj 3A: High current, high accuracy, low-dropout 3 amp voltage regulator. Pin 1 = Enable, 2 = Input, 3 = Ground, 4 = Output, 5 = Adjust
  Molex 3 Pin header 3.96mm: MOLEX 09-65-2038 WIRE-BOARD CONNECTOR HEADER 3POS, 3.96MM SPOX
  Molex Sabre 2 Pin Power: MOLEX 43160-0102 WIRE-BOARD CONNECTOR, HEADER, 2POS 7.5MM. The Sabre™ Power Connector system is ideal for robust, higher-current applications, which require design flexibility for wire- to-wire and wire-to-board configurations in both vertical and right-angle orientations. Sabre provides current ratings up to 18.0A per circuit at 600V and is available in a wide range of wire gauges and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
